// Logisim project SomadorCIs.circ as structural Verilog: 1 circuit, main circuit main
module main (
);

  wire n7486_1_pin1, n7486_1_pin2;
  wire [0:0] undriven;
  wire [3:0] n7486_1_pin11, n7486_1_pin12, n7486_1_pin13;

  Hex_Digit_Display hex_digit_display_1 (.value({3'b000, undriven[0]}));  // open: dp
  Hex_Digit_Display hex_digit_display_2 (.value(n7486_1_pin11));  // open: dp
  _7486 u_7486_1 (
    .pin1(n7486_1_pin1), .pin2(n7486_1_pin2), .pin3(n7486_1_pin11[1]), .pin13(n7486_1_pin13[0]),
    .pin12(n7486_1_pin12[0]), .pin11(n7486_1_pin11[0]), .pin10(n7486_1_pin13[1]), .pin9(n7486_1_pin12[1]),
    .pin8(n7486_1_pin1));  // open: pin4, pin5, pin6
  _7408 u_7408_1 (
    .pin13(n7486_1_pin13[0]), .pin12(n7486_1_pin12[0]), .pin11(n7486_1_pin2));  // open: pin1, pin2, pin3, pin4, pin5, pin6, pin10, pin9, pin8
  _7486 u_7486_2 ();  // open: pin1, pin2, pin3, pin4, pin5, pin6, pin13, pin12, pin11, pin10, pin9, pin8
  Slider #(.width(4), .value('hf)) INPUT_A (.out(n7486_1_pin13));
  Slider #(.width(4)) INPUT_B (.out(n7486_1_pin12));
  _7408 u_7408_2 ();  // open: pin1, pin2, pin3, pin4, pin5, pin6, pin13, pin12, pin11, pin10, pin9, pin8
  _7432 u_7432_1 ();  // open: pin1, pin2, pin3, pin4, pin5, pin6, pin13, pin12, pin11, pin10, pin9, pin8

  // Notes on the sheet:
  //   OUTPUT
endmodule
